# Fritzing sketch arduino (saved by Fritzing 0.9.3b)
breadboards: 1

parts:
  T1 = LM35 Temperature Sensor [package="TO92 [THT]"]
  Part1 = Arduino Ethernet Shield (Rev3)
  Part2 = FC-28 Soil Hygrometer Module
  Part3 = FC-28 Soil Hygrometer Module - Probe
  YL-83_-_Detection_Board1 = YL-83 Rain Sensor - Detection Board
  YL-83_-_Control_Board1 = YL-83 Rain Sensor - Control Board

nets:
  VCC: T1.+Vs, Part1.5V, Part2.VCC, YL-83_-_Control_Board1.VCC
  N1: T1.Vout, Part1.A1
  GND: T1.GND, Part1.GND, Part2.GND, YL-83_-_Control_Board1.GND
  N2: Part1.A0, Part2.AO
  N3: Part1.PWM_D5, YL-83_-_Control_Board1.AO
  N4: Part2.POS, Part3.POS
  N5: Part2.NEG, Part3.NEG
  N6: YL-83_-_Detection_Board1.POS, YL-83_-_Control_Board1.POS
  N7: YL-83_-_Detection_Board1.NEG, YL-83_-_Control_Board1.NEG

custom parts:
  FC-28 Soil Hygrometer Module: The FC-28 is a soil hygrometer module that uses the Texas Instruments LM393 comparator chip to provide an analog measurement of soil humidity. The digital output is high when soil moisture is over a certain threshold, as determined by adjusting the potentiometer.
  FC-28 Soil Hygrometer Module - Probe: The FC-28 is a soil hygrometer module that uses the Texas Instruments LM393 comparator chip to provide an analog measurement of soil humidity.
  YL-83 Rain Sensor - Detection Board: The YL-83 is a rain sensor that has more resistance when dry and less resistance when wet. The module runs at 5V.
  YL-83 Rain Sensor - Control Board: The YL-83 is a rain sensor that has more resistance when dry and less resistance when wet. The module runs at 5V.
